# Fritzing sketch SHT-21_Light_Sensor_168 (saved by Fritzing 0.9.9b)
circuit board: 8.46667cm x 5.64444cm
breadboards: 1

parts:
  Arduino1 = Arduino Mini (Rev5)
  M1 = fc-51 [package=THT]
  Součástka1 = NRF24L01+ Breakout Board
  Součástka3 = DC-DC Power Module (5v)
  Součástka2 = Barometric Pressure Sensor - BMP180 Breakout (GY-68)

nets (from the breadboard view):
  N1: Arduino1.D2, Součástka1.IRQ
  N2: Arduino1.D4, M1.pin1
  N3: Arduino1.D9_PWM, Součástka1.CE
  GND: Arduino1.GND, M1.pin2, Součástka1.GND, Součástka3.GND, Součástka2.GND
  5V: Arduino1.5V, M1.pin3, Součástka3.Vin, Součástka2.VCC
  N4: Arduino1.D13, Součástka1.SCK
  N5: Arduino1.D12, Součástka1.MISO
  N6: Arduino1.D11_PWM, Součástka1.MOSI
  N7: Arduino1.D10_PWM, Součástka1.CS
  N8: Arduino1.A4, Součástka2.SDA
  N9: Arduino1.A5, Součástka2.SCL
  N10: Součástka1.VCC, Součástka3.Vout

custom parts:
  DC-DC Power Module (5v): DC-DC Power Module based con AMS1117-5.0 Input: DC 6~12V (input power must higher 1V than output power); Output: 5V (+/-0.05V error), 800mA
