# Fritzing sketch TA12-100-energy_168 (saved by Fritzing 0.9.9b)
circuit board: 8.46667cm x 5.64444cm
breadboards: 1

parts:
  Arduino1 = Arduino Mini (Rev5)
  Součástka1 = NRF24L01+ Breakout Board
  Součástka3 = DC-DC Power Module (5v)
  TA12-100 = Inductor [package="0805 [SMD]"]

nets (from the breadboard view):
  N1: Arduino1.D2, Součástka1.IRQ
  N2: Arduino1.D9_PWM, Součástka1.CE
  GND: Arduino1.GND, Součástka1.GND, Součástka3.GND, TA12-100.pin_1
  5V: Arduino1.5V, Součástka3.Vin
  N3: Arduino1.A0, TA12-100.pin_0
  N4: Arduino1.D13, Součástka1.SCK
  N5: Arduino1.D12, Součástka1.MISO
  N6: Arduino1.D11_PWM, Součástka1.MOSI
  N7: Arduino1.D10_PWM, Součástka1.CS
  N8: Součástka1.VCC, Součástka3.Vout

custom parts:
  DC-DC Power Module (5v): DC-DC Power Module based con AMS1117-5.0 Input: DC 6~12V (input power must higher 1V than output power); Output: 5V (+/-0.05V error), 800mA
